# Fritzing sketch Button_Schema (saved by Fritzing 0.9.10b)

parts:
  U1 = ESP32-38PinWide [part_number=ESP32-38PinWide]
  S1 = Round Pushbutton
  R1 = Resistor [tolerance=±5% power=0.25 resistance=100k package=THT]

nets:
  N1: U1.3.3, S1.leg1
  N2: U1.GPIO33, S1.leg0, R1.Pin_0
  N3: U1.GND, R1.Pin_1

notes:
  100kΩ
  3v3
  33
  GND

custom parts:
  ESP32-38PinWide: Generic 38-Pin ESP32 with wide format (only access to one side of pins on a breadboard) based on Stephen Lilley's HiLetgo ESP-WROOM-32 ESP32 ESP-32S Development Board.
