# Fritzing sketch DFPlayer_Schema (saved by Fritzing 0.9.10b)

parts:
  U2 = ESP32-38PinWide [part_number=ESP32-38PinWide]
  SP1 = SPEAKER [package=pcb_mount_speaker]
  DFRobot_DFPlayer_Mini1 = DFRobot DFPlayer Mini [part_number=DFR0299]
  R1 = Resistor [tolerance=±5% power=0.25 resistance=100k package=THT]  # not connected

nets:
  VIN: U2.VIN, DFRobot_DFPlayer_Mini1.VCC
  N1: U2.GPIO16, DFRobot_DFPlayer_Mini1.TX
  N2: U2.GPIO17, DFRobot_DFPlayer_Mini1.RX
  N3: U2.GND, DFRobot_DFPlayer_Mini1.GND-1
  N4: SP1.+, DFRobot_DFPlayer_Mini1.SPK_2
  N5: SP1.-, DFRobot_DFPlayer_Mini1.SPK_1

notes:
  VCC
  RX
  TX
  SPK_2
  SPK_1
  GND
  100KΩ
  16
  17
  5V

custom parts:
  ESP32-38PinWide: Generic 38-Pin ESP32 with wide format (only access to one side of pins on a breadboard) based on Stephen Lilley's HiLetgo ESP-WROOM-32 ESP32 ESP-32S Development Board.
