# Fritzing sketch Display_7_Seg_Schema (saved by Fritzing 0.9.10b)

parts:
  Bauteil1 = 0.56" 7-segment LED Backpack [part_number=881]
  U1 = ESP32-38PinWide [part_number=ESP32-38PinWide]
  Bauteil2 = 0.56" 7-segment LED Backpack [part_number=881]  # not connected

nets:
  N1: Bauteil1.SCL, U1.GPIO22
  N2: Bauteil1.SDA, U1.GPIO21
  GND: Bauteil1.GND, U1.GND
  N3: Bauteil1.VDD, U1.3.3

notes:
  Display 1
  Display 2
  Kontakte A0 Brücke setzen
  GND
  21
  22
  3v3

custom parts:
  0.56" 7-segment LED Backpack: This 0.56" 7-segment LED display includes a driver chip for simple control via an I2C interface. The backpack features address-selection jumpers so you can connect up to eight displays on a single I2C bus.
  ESP32-38PinWide: Generic 38-Pin ESP32 with wide format (only access to one side of pins on a breadboard) based on Stephen Lilley's HiLetgo ESP-WROOM-32 ESP32 ESP-32S Development Board.
