# Fritzing sketch Display_Alles (saved by Fritzing 0.9.10b)

parts:
  Bauteil1 = 0.56" 7-segment LED Backpack [part_number=881]
  U1 = ESP32-38PinWide [part_number=ESP32-38PinWide]
  Bauteil2 = 0.56" 7-segment LED Backpack [part_number=881]  # not connected
  IC1 = 2.8 inch LCD SPI display with touch screen & SD card
  DFRobot_DFPlayer_Mini2 = DFRobot DFPlayer Mini [part_number=DFR0299]
  SP2 = SPEAKER [package=pcb_mount_speaker]
  R2 = Resistor [tolerance=±5% power=0.25 resistance=100k package=THT]  # not connected

nets:
  N1: Bauteil1.SCL, U1.GPIO22
  N2: Bauteil1.SDA, U1.GPIO21
  GND: Bauteil1.GND, U1.GND
  N3: Bauteil1.VDD, U1.3.3, IC1.pin1
  N4: U1.GPIO25, IC1.pin_9
  VIN: U1.VIN, DFRobot_DFPlayer_Mini2.VCC
  N5: U1.GPIO15, IC1.pin3
  N6: U1.GPIO2, IC1.pin5
  N7: U1.GPIO4, IC1.pin4
  N8: U1.GPIO16, DFRobot_DFPlayer_Mini2.TX
  N9: U1.GPIO17, DFRobot_DFPlayer_Mini2.RX
  N10: U1.GPIO18, IC1.pin7
  N11: U1.GPIO23, IC1.pin6
  N12: DFRobot_DFPlayer_Mini2.SPK_1, SP2.-
  N13: DFRobot_DFPlayer_Mini2.SPK_2, SP2.+

notes:
  Display 1
  Display 2
  Kontakte A0 Brücke setzen
  GND
  21
  22
  3v3
  VCC
  CS
  Reset
  D/C
  SDI(MOSI)
  SCK
  LED
  SOI(MISO)
  T_CLK
  T_CS
  T_DN
  T_OUT
  T_IRQ
  23
  18
  4
  2
  15
  25
  RX
  TX
  SPK_1
  SPK_2

custom parts:
  0.56" 7-segment LED Backpack: This 0.56" 7-segment LED display includes a driver chip for simple control via an I2C interface. The backpack features address-selection jumpers so you can connect up to eight displays on a single I2C bus.
  ESP32-38PinWide: Generic 38-Pin ESP32 with wide format (only access to one side of pins on a breadboard) based on Stephen Lilley's HiLetgo ESP-WROOM-32 ESP32 ESP-32S Development Board.
  2.8 inch LCD SPI display with touch screen & SD card: A generic 2.8 inch LCD TFT 320x280 display with touchscreen and SD card slot.
