# Fritzing sketch Display_ILI9341 (saved by Fritzing 0.9.10b)

parts:
  U1 = ESP32-38PinWide [part_number=ESP32-38PinWide]
  IC1 = 2.8 inch LCD SPI display with touch screen & SD card

nets:
  N1: U1.3.3, IC1.pin1
  N2: U1.GPIO25, IC1.pin_9
  N3: U1.GPIO15, IC1.pin3
  N4: U1.GPIO2, IC1.pin5
  N5: U1.GPIO4, IC1.pin4
  N6: U1.GPIO18, IC1.pin7
  N7: U1.GND, IC1.pin2
  N8: U1.GPIO23, IC1.pin6

notes:
  GND
  21
  22
  3v3
  VCC
  CS
  Reset
  D/C
  SDI(MOSI)
  SCK
  LED
  SOI(MISO)
  T_CLK
  T_CS
  T_DN
  T_OUT
  T_IRQ
  23
  18
  4
  2
  15
  25

custom parts:
  ESP32-38PinWide: Generic 38-Pin ESP32 with wide format (only access to one side of pins on a breadboard) based on Stephen Lilley's HiLetgo ESP-WROOM-32 ESP32 ESP-32S Development Board.
  2.8 inch LCD SPI display with touch screen & SD card: A generic 2.8 inch LCD TFT 320x280 display with touchscreen and SD card slot.
